# Fritzing sketch birdcage (saved by Fritzing 0.9.10b)
stripboards: 1

parts:
  J1 = female pin header, 2 pins [form="♀ (female)"]
  J2 = female pin header, 2 pins [form="♀ (female)"]
  J3 = female pin header, 2 pins [form="♀ (female)"]
  J4 = female pin header, 2 pins [form="♀ (female)"]
  J5 = female pin header, 2 pins [form="♀ (female)"]
  J6 = female pin header, 2 pins [form="♀ (female)"]
  J7 = female pin header, 2 pins [form="♀ (female)"]
  J8 = female pin header, 2 pins [form="♀ (female)"]
  J9 = female pin header, 2 pins [form="♀ (female)"]
  J10 = female pin header, 2 pins [form="♀ (female)"]
  J11 = female pin header, 2 pins [form="♀ (female)"]
  J12 = female pin header, 2 pins [form="♀ (female)"]
  J13 = female pin header, 2 pins [form="♀ (female)"]
  J14 = female pin header, 2 pins [form="♀ (female)"]
  J15 = female pin header, 2 pins [form="♀ (female)"]
  J16 = female pin header, 2 pins [form="♀ (female)"]
  J17 = female pin header, 2 pins [form="♀ (female)"]
  J18 = female pin header, 2 pins [form="♀ (female)"]
  J19 = female pin header, 2 pins [form="♀ (female)"]
  J20 = female pin header, 2 pins [form="♀ (female)"]
  J21 = female pin header, 2 pins [form="♀ (female)"]
  J22 = female pin header, 2 pins [form="♀ (female)"]
  J23 = female pin header, 2 pins [form="♀ (female)"]
  J24 = female pin header, 2 pins [form="♀ (female)"]
  J25 = female pin header, 2 pins [form="♀ (female)"]
  J26 = female pin header, 2 pins [form="♀ (female)"]
  J27 = female pin header, 2 pins [form="♀ (female)"]
  J28 = female pin header, 2 pins [form="♀ (female)"]
  J29 = female pin header, 2 pins [form="♀ (female)"]
  J30 = female pin header, 2 pins [form="♀ (female)"]
  J31 = female pin header, 2 pins [form="♀ (female)"]
  J32 = female pin header, 2 pins [form="♀ (female)"]
  LED1 = LED - 5mm [color="Green (570nm)" current=0.030 package="5 mm [THT]"]
  R1 = Resistor [tolerance=±5% power=0.25 resistance=330 package=THT]
  R2 = Resistor [tolerance=±5% power=0.25 resistance=330 package=THT]
  R3 = Resistor [tolerance=±5% power=0.25 resistance=330 package=THT]
  R4 = Resistor [tolerance=±5% power=0.25 resistance=330 package=THT]
  R5 = Resistor [tolerance=±5% power=0.25 resistance=330 package=THT]
  R6 = Resistor [tolerance=±5% power=0.25 resistance=330 package=THT]
  R7 = Resistor [tolerance=±5% power=0.25 resistance=330 package=THT]
  LED2 = LED - 5mm [color="Green (570nm)" current=0.030 package="5 mm [THT]"]
  LED3 = LED - 5mm [color="Green (570nm)" current=0.030 package="5 mm [THT]"]
  LED4 = LED - 5mm [color="Green (570nm)" current=0.030 package="5 mm [THT]"]
  LED5 = LED - 5mm [color="Green (570nm)" current=0.030 package="5 mm [THT]"]
  LED6 = LED - 5mm [color="Green (570nm)" current=0.030 package="5 mm [THT]"]
  LED7 = LED - 5mm [color="Green (570nm)" current=0.030 package="5 mm [THT]"]
  R8 = Resistor [tolerance=±5% power=0.25 resistance=1k package=THT]
  R10 = Resistor [tolerance=±5% power=0.25 resistance=330 package=THT]
  R11 = Resistor [tolerance=±5% power=0.25 resistance=330 package=THT]
  R12 = Resistor [tolerance=±5% power=0.25 resistance=330 package=THT]
  R13 = Resistor [tolerance=±5% power=0.25 resistance=330 package=THT]
  R14 = Resistor [tolerance=±5% power=0.25 resistance=330 package=THT]
  R15 = Resistor [tolerance=±5% power=0.25 resistance=330 package=THT]
  R16 = Resistor [tolerance=±5% power=0.25 resistance=330 package=THT]
  LED8 = LED - 5mm [color="Green (570nm)" current=0.030 package="5 mm [THT]"]
  LED9 = LED - 5mm [color="Green (570nm)" current=0.030 package="5 mm [THT]"]
  LED10 = LED - 5mm [color="Green (570nm)" current=0.030 package="5 mm [THT]"]
  LED11 = LED - 5mm [color="Green (570nm)" current=0.030 package="5 mm [THT]"]
  LED12 = LED - 5mm [color="Green (570nm)" current=0.030 package="5 mm [THT]"]
  LED13 = LED - 5mm [color="Green (570nm)" current=0.030 package="5 mm [THT]"]
  LED14 = LED - 5mm [color="Green (570nm)" current=0.030 package="5 mm [THT]"]
  S1 = Pushbutton [package="[THT]"]
  Part1 = Arduino Mega 2560 (Rev3)

nets:
  N1: J1.pin1, J1.pin2, J2.pin1, J2.pin2, J3.pin1, J3.pin2, J4.pin1, J4.pin2
  N2: J5.pin1, J5.pin2, J6.pin1, J6.pin2, Part1.A1
  N3: J7.pin1, J7.pin2, J8.pin1, J8.pin2, Part1.A6
  N4: J9.pin1, J9.pin2, J10.pin1, J10.pin2, Part1.A8
  N5: J11.pin1, J11.pin2, J12.pin1, J12.pin2, Part1.A13
  N6: J13.pin1, J13.pin2, J15.pin1, J15.pin2, Part1.A2
  N7: J14.pin1, J14.pin2, J16.pin1, J16.pin2, Part1.A5
  N8: J17.pin1, J17.pin2, J18.pin1, J18.pin2, Part1.A9
  N9: J19.pin1, J19.pin2, J20.pin1, J20.pin2, Part1.A12
  N10: J21.pin1, J21.pin2, J22.pin1, J22.pin2, Part1.A3
  N11: J23.pin1, J23.pin2, J24.pin1, J24.pin2, Part1.A4
  N12: J25.pin1, J25.pin2, J26.pin1, J26.pin2, Part1.A10
  N13: J27.pin1, J27.pin2, J28.pin1, J28.pin2, Part1.A11
  N14: J29.pin1, J29.pin2, J30.pin1, J30.pin2, J31.pin1, J31.pin2, J32.pin1, J32.pin2, R8.Pin_1, Part1.A15
  N15: LED1.cathode, LED2.cathode, LED3.cathode, LED4.cathode, LED5.cathode, LED6.cathode, LED7.cathode, R8.Pin_0, LED8.cathode, LED9.cathode, LED10.cathode, LED11.cathode, LED12.cathode, LED13.cathode, LED14.cathode, S1.Pin_3, S1.Pin_4, Part1.GND
  N16: LED1.anode, R1.Pin_0
  N17: R1.Pin_1, Part1.D35
  N18: R2.Pin_0, LED2.anode
  N19: R2.Pin_1, Part1.D33
  N20: R3.Pin_0, LED3.anode
  N21: R3.Pin_1, Part1.D31
  N22: R4.Pin_0, LED4.anode
  N23: R4.Pin_1, Part1.D29
  N24: R5.Pin_0, LED5.anode
  N25: R5.Pin_1, Part1.D27
  N26: R6.Pin_0, LED6.anode
  N27: R6.Pin_1, Part1.D25
  N28: R7.Pin_0, LED7.anode
  N29: R7.Pin_1, Part1.D23
  N30: R10.Pin_0, LED9.anode
  N31: R10.Pin_1, Part1.D41
  N32: R11.Pin_0, LED8.anode
  N33: R11.Pin_1, Part1.D39
  N34: R12.Pin_0, LED10.anode
  N35: R12.Pin_1, Part1.D43
  N36: R13.Pin_0, LED11.anode
  N37: R13.Pin_1, Part1.D45
  N38: R14.Pin_0, LED12.anode
  N39: R14.Pin_1, Part1.D47
  N40: R15.Pin_0, LED13.anode
  N41: R15.Pin_1, Part1.D49
  N42: R16.Pin_0, LED14.anode
  N43: R16.Pin_1, Part1.D51
  N44: S1.Pin_1, S1.Pin_2, Part1.D8_PWM

notes:
  Note where veroboard has been cut
